# Fritzing sketch Tag Toy mini 2 (saved by Fritzing 0.9.3b)
circuit board: 2.6973cm x 6.16326cm
breadboards: 2

parts:
  ProMini = Arduino Pro Mini v13
  R1 = Resistor [tolerance=±5% resistance=1k package=THT]
  IND_RED = LED - 5mm [color="Red (633nm)" part_number=R package="5 mm [THT]"]
  R2 = Resistor [tolerance=±5% resistance=10 package=THT]
  SPKR = Loudspeaker
  IND_GRN = LED - 5mm [color="Green (560nm)" part_number=G package="5 mm [THT]"]
  MZL = LED - 5mm [color="Orange (620nm)" part_number=M package="5 mm [THT]"]
  R3 = Resistor [tolerance=±5% resistance=220 package=THT]
  R4 = Resistor [tolerance=±5% resistance=220 package=THT]
  R5 = Resistor [tolerance=±5% resistance=47 package=THT]
  VCC1 = Battery block 9V
  N = Basic FET N-Channel [package="TO220 [THT]"]
  SOUND = DFRobot DFPlayer Mini [part_number=DFR0299]
  R6 = Resistor [tolerance=±5% resistance=10 package=THT]
  PLS = LED - 5mm [color="Infrared (940nm)" package="5 mm [THT]"]
  I2C = female pin header, 2 pins [form="♀ (female)"]
  J1 = female pin header, 2 pins [form="♀ (female)"]
  FIRE = female pin header, 2 pins [form="♀ (female)"]
  RLD = female pin header, 2 pins [form="♀ (female)"]
  MODE = female pin header, 2 pins [form="♀ (female)"]

nets:
  N1: ProMini.A4, ProMini.A1, I2C.pin1
  N2: ProMini.A5, ProMini.A2, I2C.pin2
  N3: ProMini.RAW, VCC1.+, PLS.cathode
  N4: ProMini.GND, IND_RED.cathode, IND_GRN.cathode, R5.Pin_0, VCC1.-, N.source, SOUND.GND-1, SOUND.GND-2, J1.pin1, FIRE.pin1, RLD.pin1, MODE.pin1
  VCC: ProMini.VCC, SOUND.VCC, J1.pin2
  N5: ProMini.D11_PWM/MOSI, R1.Pin_0
  N6: ProMini.D10_PWM/SS, SOUND.TX
  N7: ProMini.D8, R3.Pin_0
  N8: ProMini.D7, R4.Pin_0
  N9: ProMini.D6_PWM, MZL.anode
  N10: ProMini.D5_PWM, N.gate
  N11: ProMini.D4, MODE.pin2
  N12: ProMini.D3_PWM, RLD.pin2
  N13: ProMini.D2, FIRE.pin2
  N14: R1.Pin_1, SOUND.RX
  N15: IND_RED.anode, R4.Pin_1
  N16: R2.Pin_0, SOUND.SPK_2
  N17: R2.Pin_1, SPKR.pin1
  N18: SPKR.pin2, SOUND.SPK_1
  N19: IND_GRN.anode, R3.Pin_1
  N20: MZL.cathode, R5.Pin_1
  N21: N.drain, R6.Pin_0
  N22: R6.Pin_1, PLS.anode

notes:
  LOTNA
  D Rowley 2018
  +
  -
  Tag Circuit v2
